# Fritzing sketch esp12f (saved by Fritzing 0.9.2b)
circuit board: 8.46667cm x 5.64444cm
perfboards: 1

parts:
  Nokia_5110_LCD_Module1 = pcd8544
  U1 = ESP-12F (ESP8266 WiFi Module) [part_number=ESP8266]

nets:
  N1: Nokia_5110_LCD_Module1.RST, U1.GPIO4
  N2: Nokia_5110_LCD_Module1.CE, U1.GPIO5
  N3: Nokia_5110_LCD_Module1.DC, U1.GPIO12
  N4: Nokia_5110_LCD_Module1.DIN, U1.GPIO13
  N5: Nokia_5110_LCD_Module1.CLK, U1.GPIO14
  VCC: Nokia_5110_LCD_Module1.VCC, U1.VCC
  GND: Nokia_5110_LCD_Module1.LIGHT, Nokia_5110_LCD_Module1.GND, U1.GND

custom parts:
  pcd8544: Nokia 5110 LCD with 8 pin. It's a 45mm*45mm module part. Description: The Nokia 5110 is a basic graphic LCD screen for lots of applications. It was originally intended for as a cell phone screen. This one is mounted on an easy to solder PCB. It uses the PCD8544 controller. The PCD8544 is a low power CMOS LCD controller/driver, designed to drive a graphic display of 48 rows and 84 columns. All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
  ESP-12F (ESP8266 WiFi Module): WiFi Module based on the ESP8266 with onboard PCB antenna and UART communications
